// Logisim project 2 Bit Counter.circ as structural Verilog: 1 circuit, main circuit main
module main (
);

  wire and_1_out, and_2_out, clock_1_out, d_ff_1_q, d_ff_2_q, not_1_out, not_2_out, not_3_out, or_1_out,
       undriven;

  or or_1 (or_1_out, and_1_out, and_2_out, not_3_out, not_3_out, not_3_out);
  and and_1 (and_1_out, not_1_out, d_ff_1_q, 1'b1, 1'b1, 1'b1);
  and and_2 (and_2_out, d_ff_2_q, not_2_out, 1'b1, 1'b1, 1'b1);
  Clock clock_1 (.out(clock_1_out));
  D_Flip_Flop d_ff_1 (.clk(clock_1_out), .D(not_2_out), .Q(d_ff_1_q), .en(1'b1));  // open: Qn, preset, reset
  not not_1 (not_1_out, d_ff_2_q);
  D_Flip_Flop d_ff_2 (.clk(clock_1_out), .D(or_1_out), .Q(d_ff_2_q), .preset(undriven), .en(1'b1));  // open: Qn, reset
  not not_2 (not_2_out, d_ff_1_q);
  LED led_1 (.in(d_ff_1_q));
  LED led_2 (.in(d_ff_2_q));
  not not_3 (not_3_out, 1'b1);
endmodule
