// Logisim project 3 Bit Counter and Pattern Generator.circ as structural Verilog: 1 circuit, main circuit main
module main (
);

  wire and_1_out, and_2_out, and_3_out, and_4_out, and_5_out, and_6_out, and_7_out, and_8_out, button_1_out,
       clock_1_out, not_1_out, not_2_out, not_3_out, or_1_out, or_2_out, or_3_out, register_1_q,
       register_2_q, register_3_q;

  LED led_1 (.in(register_1_q));
  LED led_2 (.in(register_2_q));
  LED led_3 (.in(register_3_q));
  Clock clock_1 (.out(clock_1_out));
  Register #(.width(1)) register_1 (.D(or_1_out), .en(1'b1), .Q(register_1_q), .clk(clock_1_out), .clr(button_1_out));
  not not_1 (not_1_out, register_1_q);
  Register #(.width(1)) register_2 (.D(or_2_out), .en(1'b1), .Q(register_2_q), .clk(clock_1_out), .clr(button_1_out));
  not not_2 (not_2_out, register_3_q);
  not not_3 (not_3_out, register_2_q);
  Register #(.width(1)) register_3 (.D(not_2_out), .en(1'b1), .Q(register_3_q), .clk(clock_1_out), .clr(button_1_out));
  and and_1 (and_1_out, register_1_q, not_3_out);
  and and_2 (and_2_out, not_1_out, register_2_q, register_3_q);
  and and_3 (and_3_out, register_1_q, not_2_out);
  and and_4 (and_4_out, not_3_out, register_3_q);
  and and_5 (and_5_out, register_2_q, not_2_out);
  and and_6 (and_6_out, register_1_q, not_2_out);
  and and_7 (and_7_out, not_1_out, not_3_out, register_3_q);
  and and_8 (and_8_out, register_1_q, register_2_q);
  Button button_1 (.out(button_1_out));
  or or_1 (or_1_out, and_1_out, and_2_out, and_3_out);
  or or_2 (or_2_out, and_4_out, and_5_out);
  or or_3 (or_3_out, and_6_out, and_7_out, and_8_out);
  LED led_4 (.in(or_3_out));
endmodule
