// Logisim project 8 Bit Manual Adder and Subber.circ as structural Verilog: 1 circuit, main circuit main
module main (
  input  [7:0] in_1,
  input  in_2,
  input  in_3,
  input  in_4,
  input  in_5,
  input  in_6,
  input  in_7,
  input  in_8,
  input  in_9,
  input  in_10,
  input  in_11,
  output [7:0] out_12,
  output [7:0] out_13,
  output [7:0] out_14,
  output [7:0] out_15,
  output [7:0] out_16
);

  wire bitselector_1_out, button_1_out, button_2_out, button_3_out, button_4_out, clock_1_out;
  wire [7:0] adder_1_out, multiplexer_1_out, subtractor_1_out;

  Clock clock_1 (.out(clock_1_out));
  Button button_1 (.out(button_1_out));
  Button button_2 (.out(button_2_out));
  Button button_3 (.out(button_3_out));
  Button button_4 (.out(button_4_out));
  Register register_1 (.D(out_16), .en(in_3), .Q(out_12), .clk(clock_1_out), .clr(button_1_out));
  Register register_2 (.D(out_16), .en(in_5), .Q(out_13), .clk(clock_1_out), .clr(button_2_out));
  Register register_3 (.D(out_16), .en(in_7), .Q(out_14), .clk(clock_1_out), .clr(button_3_out));
  Register register_4 (.D(out_16), .en(in_9), .Q(out_15), .clk(clock_1_out), .clr(button_4_out));
  assign out_16 = in_4 ? out_12 : 8'bz;  // Controlled_Buffer controlled_buffer_1
  assign out_16 = in_6 ? out_13 : 8'bz;  // Controlled_Buffer controlled_buffer_2
  assign out_16 = in_8 ? out_14 : 8'bz;  // Controlled_Buffer controlled_buffer_3
  assign out_16 = in_10 ? out_15 : 8'bz;  // Controlled_Buffer controlled_buffer_4
  assign out_16 = in_2 ? in_1 : 8'bz;  // Controlled_Buffer controlled_buffer_5
  Adder adder_1 (.a(out_12), .b(out_13), .out(adder_1_out));  // open: cin, cout
  Subtractor subtractor_1 (.a(out_12), .b(out_13), .out(subtractor_1_out));  // open: bin, bout
  BitSelector bitselector_1 (.in(out_14), .out(bitselector_1_out), .sel(3'b000));
  assign out_16 = in_11 ? multiplexer_1_out : 8'bz;  // Controlled_Buffer controlled_buffer_6
  Multiplexer #(.width(8), .enable("false")) multiplexer_1 (
    .in0(adder_1_out), .in1(subtractor_1_out), .out(multiplexer_1_out), .sel(bitselector_1_out));
  LED led_1 ();  // open: in

  // Notes on the sheet:
  //   A Register Read Write Reset
  //   B Register Read Write Reset
  //   Operation Register Read Write Reset
  //   D Register Read Write Reset
  //   Adder and Subber Write
  //   Bus Write
endmodule
