// Logisim project 8 Bit Register System.circ as structural Verilog: 1 circuit, main circuit main
module main (
  input  [7:0] in_1,
  input  in_2,
  input  in_3,
  input  in_4,
  input  in_5,
  input  in_6,
  input  in_7,
  input  in_8,
  input  in_9,
  input  in_10,
  output [7:0] out_11,
  output [7:0] out_12,
  output [7:0] out_13,
  output [7:0] out_14,
  output [7:0] out_15
);

  wire button_1_out, button_2_out, button_3_out, button_4_out, clock_1_out;

  Button button_1 (.out(button_1_out));
  Button button_2 (.out(button_2_out));
  Button button_3 (.out(button_3_out));
  Button button_4 (.out(button_4_out));
  Clock clock_1 (.out(clock_1_out));
  assign out_15 = in_4 ? out_11 : 8'bz;  // Controlled_Buffer controlled_buffer_1
  Register register_1 (.D(out_15), .en(in_3), .Q(out_11), .clk(clock_1_out), .clr(button_1_out));
  assign out_15 = in_6 ? out_12 : 8'bz;  // Controlled_Buffer controlled_buffer_2
  Register register_2 (.D(out_15), .en(in_5), .Q(out_12), .clk(clock_1_out), .clr(button_2_out));
  Register register_3 (.D(out_15), .en(in_7), .Q(out_13), .clk(clock_1_out), .clr(button_3_out));
  assign out_15 = in_8 ? out_13 : 8'bz;  // Controlled_Buffer controlled_buffer_3
  assign out_15 = in_10 ? out_14 : 8'bz;  // Controlled_Buffer controlled_buffer_4
  Register register_4 (.D(out_15), .en(in_9), .Q(out_14), .clk(clock_1_out), .clr(button_4_out));
  assign out_15 = in_2 ? in_1 : 8'bz;  // Controlled_Buffer controlled_buffer_5
  LED led_1 ();  // open: in
endmodule
