// Logisim project Blinker With Enable.circ as structural Verilog: 1 circuit, main circuit main
module main (
);

  wire and_1_out, and_2_out, and_3_out, and_4_out, button_1_out, clock_1_out, not_1_out, not_2_out,
       not_3_out, or_1_out, register_1_q, register_2_q;

  Clock clock_1 (.out(clock_1_out));
  LED led_1 (.in(register_1_q));
  Register #(.width(1)) register_1 (.D(or_1_out), .en(1'b1), .Q(register_1_q), .clk(clock_1_out));  // open: clr
  LED led_2 (.in(register_2_q));
  not not_1 (not_1_out, register_1_q);
  not not_2 (not_2_out, register_2_q);
  Register #(.width(1)) register_2 (.D(and_4_out), .en(1'b1), .Q(register_2_q), .clk(clock_1_out));  // open: clr
  LED led_3 (.in(button_1_out));
  not not_3 (not_3_out, button_1_out);
  Button button_1 (.out(button_1_out));
  and and_1 (and_1_out, register_1_q, not_2_out);
  and and_2 (and_2_out, register_1_q, button_1_out);
  and and_3 (and_3_out, not_2_out, button_1_out);
  and and_4 (and_4_out, register_1_q, not_2_out);
  or or_1 (or_1_out, and_1_out, and_2_out, and_3_out);
  LED led_4 (.in(and_4_out));
endmodule
