// Logisim project 3 Bit Supercomputer.circ as structural Verilog: 1 circuit, main circuit main
module main (
);

  wire adder_1_cout, adder_1_out, adder_2_cout, adder_2_out, adder_3_cout, adder_3_out, button_1_out,
       button_2_out, clock_1_out, register_1_q, register_2_q, register_3_q, register_4_q, register_5_q,
       register_6_q, undriven, undriven_2, undriven_3, undriven_4, undriven_5, undriven_6;

  Clock clock_1 (.out(clock_1_out));
  LED led_1 (.in(register_1_q));
  LED led_2 (.in(register_2_q));
  Register #(.width(1)) register_1 (
    .D(adder_1_out), .en(1'b1), .Q(register_1_q), .clk(clock_1_out), .clr(button_1_out));
  Button button_1 (.out(button_1_out));
  LED led_3 (.in(register_3_q));
  Register #(.width(1)) register_2 (
    .D(adder_2_out), .en(1'b1), .Q(register_2_q), .clk(clock_1_out), .clr(button_1_out));
  Adder #(.width(1)) adder_1 (
    .a(register_1_q), .b(undriven), .out(adder_1_out), .cin(adder_2_cout), .cout(adder_1_cout));
  Register #(.width(1)) register_3 (
    .D(adder_3_out), .en(1'b1), .Q(register_3_q), .clk(clock_1_out), .clr(button_1_out));
  Adder #(.width(1)) adder_2 (
    .a(register_2_q), .b(undriven_2), .out(adder_2_out), .cin(adder_3_cout), .cout(adder_2_cout));
  LED led_4 (.in(register_4_q));
  LED led_5 (.in(register_5_q));
  Button button_2 (.out(button_2_out));
  Adder #(.width(1)) adder_3 (.a(register_3_q), .b(undriven_4), .out(adder_3_out), .cout(adder_3_cout));  // open: cin
  LED led_6 (.in(register_6_q));
  Register #(.width(1)) register_4 (.D(undriven_5), .en(1'b1), .Q(register_4_q), .clk(clock_1_out), .clr(button_2_out));
  Register #(.width(1)) register_5 (.D(undriven_3), .en(1'b1), .Q(register_5_q), .clk(clock_1_out), .clr(button_2_out));
  Register #(.width(1)) register_6 (.D(undriven_6), .en(1'b1), .Q(register_6_q), .clk(clock_1_out), .clr(button_2_out));
endmodule
