// Logisim project 4 Bit Adder.circ as structural Verilog: 1 circuit, main circuit main
module main (
  input  in_1,
  input  in_2,
  input  in_3,
  input  in_4,
  input  in_5,
  input  in_6
);

  wire adder_1_cout, adder_1_out, adder_2_cout, adder_2_out, adder_3_cout, adder_3_out;

  Adder #(.width(1)) adder_1 (.a(in_3), .b(in_6), .out(adder_1_out), .cin(1'b0), .cout(adder_1_cout));
  Adder #(.width(1)) adder_2 (.a(in_2), .b(in_5), .out(adder_2_out), .cin(adder_1_cout), .cout(adder_2_cout));
  Adder #(.width(1)) adder_3 (.a(in_1), .b(in_4), .out(adder_3_out), .cin(adder_2_cout), .cout(adder_3_cout));
  LED led_1 (.in(adder_3_cout));
  LED led_2 (.in(adder_3_out));
  LED led_3 (.in(adder_2_out));
  LED led_4 (.in(adder_1_out));
endmodule
