// Logisim project 4 Bit Computer.circ as structural Verilog: 1 circuit, main circuit main
module main (
  input  in_1,
  input  in_2,
  input  in_3,
  input  in_4,
  input  in_5,
  input  in_6,
  input  in_7,
  input  in_8,
  input  in_9,
  input  in_10,
  input  in_11,
  input  in_12
);

  wire adder_1_cout, adder_1_out, adder_2_cout, adder_2_out, adder_3_cout, adder_3_out, adder_4_cout,
       adder_4_out, button_1_out, button_2_out, button_3_out, clock_1_out, controlled_buffer_1_out,
       controlled_buffer_2_out, controlled_buffer_3_out, controlled_buffer_4_out, register_1_q, register_2_q,
       register_3_q, register_4_q, register_5_q, register_6_q, register_7_q, register_8_q, register_9_q,
       register_10_q, register_11_q, register_12_q;

  Clock clock_1 (.out(clock_1_out));
  Button button_1 (.out(button_1_out));
  Button button_2 (.out(button_2_out));
  Button button_3 (.out(button_3_out));
  Register #(.width(1)) register_1 (
    .D(controlled_buffer_1_out), .en(in_2), .Q(register_1_q), .clk(clock_1_out), .clr(button_1_out));
  Register #(.width(1)) register_2 (
    .D(controlled_buffer_1_out), .en(in_4), .Q(register_2_q), .clk(clock_1_out), .clr(button_2_out));
  Register #(.width(1)) register_3 (
    .D(controlled_buffer_1_out), .en(in_11), .Q(register_3_q), .clk(clock_1_out), .clr(button_3_out));
  Register #(.width(1)) register_4 (
    .D(controlled_buffer_2_out), .en(in_2), .Q(register_4_q), .clk(clock_1_out), .clr(button_1_out));
  Register #(.width(1)) register_5 (
    .D(controlled_buffer_3_out), .en(in_2), .Q(register_5_q), .clk(clock_1_out), .clr(button_1_out));
  Register #(.width(1)) register_6 (
    .D(controlled_buffer_3_out), .en(in_4), .Q(register_6_q), .clk(clock_1_out), .clr(button_2_out));
  Register #(.width(1)) register_7 (
    .D(controlled_buffer_2_out), .en(in_4), .Q(register_7_q), .clk(clock_1_out), .clr(button_2_out));
  Register #(.width(1)) register_8 (
    .D(controlled_buffer_2_out), .en(in_11), .Q(register_8_q), .clk(clock_1_out), .clr(button_3_out));
  Register #(.width(1)) register_9 (
    .D(controlled_buffer_3_out), .en(in_11), .Q(register_9_q), .clk(clock_1_out), .clr(button_3_out));
  Register #(.width(1)) register_10 (
    .D(controlled_buffer_4_out), .en(in_2), .Q(register_10_q), .clk(clock_1_out), .clr(button_1_out));
  Register #(.width(1)) register_11 (
    .D(controlled_buffer_4_out), .en(in_4), .Q(register_11_q), .clk(clock_1_out), .clr(button_2_out));
  Register #(.width(1)) register_12 (
    .D(controlled_buffer_4_out), .en(in_11), .Q(register_12_q), .clk(clock_1_out), .clr(button_3_out));
  LED led_1 (.in(register_10_q));
  LED led_2 (.in(register_1_q));
  LED led_3 (.in(register_5_q));
  LED led_4 (.in(register_4_q));
  LED led_5 (.in(register_6_q));
  LED led_6 (.in(register_11_q));
  LED led_7 (.in(register_2_q));
  LED led_8 (.in(register_7_q));
  LED led_9 (.in(register_9_q));
  LED led_10 (.in(register_12_q));
  LED led_11 (.in(register_8_q));
  LED led_12 (.in(register_3_q));
  LED led_13 (.in(controlled_buffer_1_out));
  LED led_14 (.in(controlled_buffer_2_out));
  assign controlled_buffer_1_out = in_3 ? register_1_q : 1'bz;  // Controlled_Buffer controlled_buffer_1
  assign controlled_buffer_2_out = in_3 ? register_4_q : 1'bz;  // Controlled_Buffer controlled_buffer_2
  assign controlled_buffer_3_out = in_3 ? register_5_q : 1'bz;  // Controlled_Buffer controlled_buffer_3
  assign controlled_buffer_4_out = in_3 ? register_10_q : 1'bz;  // Controlled_Buffer controlled_buffer_4
  assign controlled_buffer_1_out = in_5 ? register_2_q : 1'bz;  // Controlled_Buffer controlled_buffer_5
  assign controlled_buffer_2_out = in_5 ? register_7_q : 1'bz;  // Controlled_Buffer controlled_buffer_6
  assign controlled_buffer_3_out = in_5 ? register_6_q : 1'bz;  // Controlled_Buffer controlled_buffer_7
  assign controlled_buffer_4_out = in_5 ? register_11_q : 1'bz;  // Controlled_Buffer controlled_buffer_8
  assign controlled_buffer_1_out = in_12 ? register_3_q : 1'bz;  // Controlled_Buffer controlled_buffer_9
  assign controlled_buffer_2_out = in_12 ? register_8_q : 1'bz;  // Controlled_Buffer controlled_buffer_10
  assign controlled_buffer_3_out = in_12 ? register_9_q : 1'bz;  // Controlled_Buffer controlled_buffer_11
  assign controlled_buffer_4_out = in_12 ? register_12_q : 1'bz;  // Controlled_Buffer controlled_buffer_12
  LED led_15 (.in(controlled_buffer_4_out));
  LED led_16 (.in(controlled_buffer_3_out));
  assign controlled_buffer_1_out = in_1 ? adder_4_out : 1'bz;  // Controlled_Buffer controlled_buffer_13
  assign controlled_buffer_2_out = in_1 ? adder_3_out : 1'bz;  // Controlled_Buffer controlled_buffer_14
  assign controlled_buffer_3_out = in_1 ? adder_2_out : 1'bz;  // Controlled_Buffer controlled_buffer_15
  assign controlled_buffer_4_out = in_1 ? adder_1_out : 1'bz;  // Controlled_Buffer controlled_buffer_16
  assign controlled_buffer_1_out = in_10 ? in_6 : 1'bz;  // Controlled_Buffer controlled_buffer_17
  assign controlled_buffer_2_out = in_10 ? in_7 : 1'bz;  // Controlled_Buffer controlled_buffer_18
  assign controlled_buffer_3_out = in_10 ? in_8 : 1'bz;  // Controlled_Buffer controlled_buffer_19
  assign controlled_buffer_4_out = in_10 ? in_9 : 1'bz;  // Controlled_Buffer controlled_buffer_20
  Adder #(.width(1)) adder_1 (
    .a(register_10_q), .b(register_11_q), .out(adder_1_out), .cout(adder_1_cout));  // open: cin
  Adder #(.width(1)) adder_2 (
    .a(register_5_q), .b(register_6_q), .out(adder_2_out), .cin(adder_1_cout), .cout(adder_2_cout));
  Adder #(.width(1)) adder_3 (
    .a(register_4_q), .b(register_7_q), .out(adder_3_out), .cin(adder_2_cout), .cout(adder_3_cout));
  Adder #(.width(1)) adder_4 (
    .a(register_1_q), .b(register_2_q), .out(adder_4_out), .cin(adder_3_cout), .cout(adder_4_cout));
  LED led_17 ();  // open: in
endmodule
