// Logisim project 4 Bit Register.circ as structural Verilog: 1 circuit, main circuit main
module main (
);

  wire button_1_out, clock_1_out, register_1_q, register_2_q, register_3_q, register_4_q, undriven,
       undriven_2, undriven_3, undriven_4;

  Button button_1 (.out(button_1_out));
  Clock clock_1 (.out(clock_1_out));
  Register #(.width(1)) register_1 (.D(undriven), .en(1'b1), .Q(register_1_q), .clk(clock_1_out), .clr(button_1_out));
  Register #(.width(1)) register_2 (.D(undriven_2), .en(1'b1), .Q(register_2_q), .clk(clock_1_out), .clr(button_1_out));
  Register #(.width(1)) register_3 (.D(undriven_3), .en(1'b1), .Q(register_3_q), .clk(clock_1_out), .clr(button_1_out));
  Register #(.width(1)) register_4 (.D(undriven_4), .en(1'b1), .Q(register_4_q), .clk(clock_1_out), .clr(button_1_out));
  LED led_1 (.in(undriven));
  LED led_2 (.in(undriven_2));
  LED led_3 (.in(undriven_3));
  LED led_4 (.in(undriven_4));
endmodule
