// Logisim project 4x8 RAM.circ as structural Verilog: 1 circuit, main circuit main
module main (
  input  [1:0] in_1,
  output [7:0] out_2,
  output [7:0] out_3,
  output [7:0] out_4,
  output [7:0] out_5,
  output [7:0] out_6
);

  wire undriven, undriven_2, undriven_3, undriven_4, undriven_5, undriven_6, undriven_7, undriven_8,
       undriven_9, undriven_10, undriven_11, undriven_12;
  wire [7:0] demultiplexer_1_out0, demultiplexer_1_out1, demultiplexer_1_out2, demultiplexer_1_out3;

  Demultiplexer #(.select(2), .width(8)) demultiplexer_1 (
    .out0(demultiplexer_1_out0), .out1(demultiplexer_1_out1), .out2(demultiplexer_1_out2),
    .out3(demultiplexer_1_out3));  // open: in, sel, en
  Register register_1 (.D(demultiplexer_1_out0), .en(undriven), .Q(out_3), .clk(undriven_2), .clr(undriven_3));
  Register register_2 (.D(demultiplexer_1_out1), .en(undriven_4), .Q(out_4), .clk(undriven_5), .clr(undriven_6));
  Register register_3 (.D(demultiplexer_1_out2), .en(undriven_7), .Q(out_5), .clk(undriven_8), .clr(undriven_9));
  Register register_4 (.D(demultiplexer_1_out3), .en(undriven_10), .Q(out_6), .clk(undriven_11), .clr(undriven_12));
  Multiplexer #(.select(2), .width(8)) multiplexer_1 (
    .in0(out_3), .in1(out_4), .in2(out_5), .in3(out_6), .out(out_2), .sel(in_1));  // open: en
endmodule
