// Logisim project EvoCPU.circ as structural Verilog: 1 circuit, main circuit main
module main (
  input  in_1,
  input  in_2,
  input  write,
  input  in_4,
  input  in_5,
  input  in_6,
  input  in_7,
  input  in_8,
  input  in_9
);

  wire button_1_out, button_2_out, button_3_out, button_4_out, clock_1_out;
  wire [7:0] adder_1_out, controlled_buffer_1_out, register_1_q, register_2_q, register_3_q, register_4_q;

  Clock clock_1 (.out(clock_1_out));
  Register register_1 (.D(controlled_buffer_1_out), .en(in_5), .clk(clock_1_out), .Q(register_1_q), .clr(button_1_out));
  Button button_1 (.out(button_1_out));
  Button button_2 (.out(button_2_out));
  Button button_3 (.out(button_3_out));
  Button button_4 (.out(button_4_out));
  Register register_2 (.D(controlled_buffer_1_out), .en(in_6), .clk(clock_1_out), .Q(register_2_q), .clr(button_2_out));
  Register register_3 (.D(controlled_buffer_1_out), .en(in_7), .clk(clock_1_out), .Q(register_3_q), .clr(button_3_out));
  Register register_4 (.D(controlled_buffer_1_out), .en(in_8), .clk(clock_1_out), .Q(register_4_q), .clr(button_4_out));
  assign controlled_buffer_1_out = in_1 ? register_1_q : 8'bz;  // Controlled_Buffer controlled_buffer_1
  assign controlled_buffer_1_out = in_2 ? register_2_q : 8'bz;  // Controlled_Buffer controlled_buffer_2
  assign controlled_buffer_1_out = write ? register_3_q : 8'bz;  // Controlled_Buffer controlled_buffer_3
  assign controlled_buffer_1_out = in_4 ? register_4_q : 8'bz;  // Controlled_Buffer controlled_buffer_4
  Adder adder_1 (.a(register_1_q), .b(register_2_q), .out(adder_1_out));  // open: cin, cout
  assign controlled_buffer_1_out = in_9 ? ~adder_1_out : 8'bz;  // Controlled_Inverter controlled_inverter_1

  // Notes on the sheet:
  //   read
  //   reset
  //   adder write
  //   accumulator
  //   buffer
  //   instruction
  //   output
endmodule
